# Fritzing sketch ir-sensor (saved by Fritzing 0.9.3b)

parts:
  Raspberry_Pi_2 = Raspberry Pi 3 [part_number=RPI-3-V1.2]
  Part1 = Max Power IR LED Kit

nets:
  GND: Raspberry_Pi_2.GND, Part1.GND
  N1: Raspberry_Pi_2.GIPO25, Part1.CONTROL
  5V: Raspberry_Pi_2.5V, Part1.VCC

notes:
  Engine
