# Fritzing sketch line-follower (saved by Fritzing 0.9.3b)
breadboards: 1

parts:
  Raspberry_Pi_2 = Raspberry Pi 3 [part_number=RPI-3-V1.2]
  IC1 = L293D [package=THT]
  M1 = DC Motor
  VCC1 = 4 x AAA Battery Mount
  M2 = DC Motor
  Part2 = Max Power IR LED Kit
  Part3 = Max Power IR LED Kit

nets:
  N1: Raspberry_Pi_2.GIPO11, Part2.CONTROL
  N2: Raspberry_Pi_2.GIPO13, IC1.In_4
  N3: Raspberry_Pi_2.GIPO19, IC1.In_3
  N4: Raspberry_Pi_2.GIPO26, IC1.Enable_2
  N5: Raspberry_Pi_2.GIPO21, IC1.Enable_1
  N6: Raspberry_Pi_2.GIPO20, IC1.In_1
  N7: Raspberry_Pi_2.GIPO16, IC1.In_2
  N8: Raspberry_Pi_2.GIPO8, Part3.CONTROL
  GND: Raspberry_Pi_2.GND, IC1.0V, VCC1.-, Part2.GND, Part3.GND
  N9: Raspberry_Pi_2.5V, IC1.+V
  N10: IC1.Out_1_(_Controlled_by_Enable_1_), M1.pin_2
  N11: IC1.Out_2_(_Controlled_by_Enable_1_), M1.pin_1
  VCC: IC1.+Vmotor, VCC1.+, Part2.VCC, Part3.VCC
  N12: IC1.Out_3_(_Controlled_by_Enable_2_), M2.pin_1
  N13: IC1.Out_4_(_Controlled_by_Enable_2_), M2.pin_2

notes:
  Engine
