# Fritzing sketch range-sensor (saved by Fritzing 0.9.3b)
breadboards: 1

parts:
  Raspberry_Pi_2 = Raspberry Pi 3 [part_number=RPI-3-V1.2]
  hc-sr1 = hc-sr04
  R1 = Resistor [tolerance=±5% resistance=4.7k package=THT]
  R2 = Resistor [tolerance=±5% resistance=10k package=THT]

nets:
  GND: Raspberry_Pi_2.GND, hc-sr1.GND, R2.Pin_1
  N1: Raspberry_Pi_2.GIPO24, R1.Pin_1
  N2: Raspberry_Pi_2.GIPO23, hc-sr1.Trig
  5V: Raspberry_Pi_2.5V, hc-sr1.VCC
  N3: hc-sr1.Echo, R1.Pin_0, R2.Pin_0

notes:
  Engine
  10k Resistor
  4.7k Resistor
